// Logisim project simple calci logism.circ as structural Verilog: 1 circuit, main circuit main
module main (
  input  a1,
  input  a0,
  input  [1:0] s1s0,
  input  b1,
  input  b0,
  input  in_6,
  input  in_7,
  input  in_8,
  input  in_9,
  input  in_10,
  input  in_11,
  output recurring,
  output y3,
  output y2,
  output y1,
  output y0
);

  wire adder_1_cout, adder_1_out, adder_2_cout, adder_2_out, adder_3_cout, adder_3_out, adder_4_cout,
       adder_4_out, adder_5_out, adder_6_cout, adder_6_out, adder_7_cout, adder_7_out, adder_8_cout,
       adder_8_out, and_1_out, and_2_out, and_3_out, and_4_out, and_5_out, and_6_out, and_7_out, and_8_out,
       and_9_out, and_10_out, and_11_out, and_12_out, and_13_out, and_14_out, multiplexer_1_out,
       multiplexer_2_out, not_1_out, not_2_out, not_3_out, not_4_out, not_5_out, not_6_out, not_7_out,
       not_8_out, not_9_out, not_10_out, not_11_out, or_1_out, or_2_out, or_3_out, or_4_out, xor_1_out;

  not not_1 (not_1_out, b0);
  not not_2 (not_2_out, b1);
  not not_3 (not_3_out, a1);
  not not_4 (not_4_out, b1);
  not not_5 (not_5_out, a0);
  not not_6 (not_6_out, b0);
  not not_7 (not_7_out, a1);
  Adder #(.width(1)) adder_1 (.a(a0), .b(b0), .out(adder_1_out), .cin(in_6), .cout(adder_1_cout));
  Adder #(.width(1)) adder_2 (.a(a0), .b(not_1_out), .out(adder_2_out), .cin(in_8), .cout(adder_2_cout));
  Adder #(.width(1)) adder_3 (.a(adder_2_out), .b(adder_7_cout), .out(adder_3_out), .cin(in_9), .cout(adder_3_cout));
  and and_1 (and_1_out, not_3_out, b1);
  xor xor_1 (xor_1_out, a1, b1);
  not not_8 (not_8_out, xor_1_out);
  not not_9 (not_9_out, a0);
  and and_2 (and_2_out, a0, b0);
  and and_3 (and_3_out, a0, b1);
  and and_4 (and_4_out, a1, b0);
  and and_5 (and_5_out, a1, not_4_out, b0);
  and and_6 (and_6_out, a0, not_4_out, b0);
  and and_7 (and_7_out, a1, b1);
  and and_8 (and_8_out, a1, not_5_out, b0);
  and and_9 (and_9_out, a0, not_6_out);
  and and_10 (and_10_out, b0, b1, not_7_out, a0);
  Adder #(.width(1)) adder_4 (.a(a1), .b(b1), .out(adder_4_out), .cin(adder_1_cout), .cout(adder_4_cout));
  Adder #(.width(1)) adder_5 (.a(adder_7_out), .b(in_9), .out(adder_5_out), .cin(adder_3_cout));  // open: cout
  Adder #(.width(1)) adder_6 (.a(and_3_out), .b(and_4_out), .out(adder_6_out), .cin(in_11), .cout(adder_6_cout));
  or or_1 (or_1_out, and_6_out, and_7_out);
  Adder #(.width(1)) adder_7 (.a(a1), .b(not_2_out), .out(adder_7_out), .cin(adder_2_cout), .cout(adder_7_cout));
  or or_2 (or_2_out, and_1_out, and_11_out);
  and and_11 (and_11_out, not_8_out, not_9_out, b0);
  and and_12 (and_12_out, b1, a1);
  or or_3 (or_3_out, and_8_out, and_9_out);
  not not_10 (not_10_out, adder_2_out);
  not not_11 (not_11_out, adder_7_out);
  Adder #(.width(1)) adder_8 (.a(adder_6_cout), .b(and_12_out), .out(adder_8_out), .cin(in_11), .cout(adder_8_cout));
  and and_13 (and_13_out, or_3_out, b1);
  or or_4 (or_4_out, and_10_out, and_13_out);
  Multiplexer #(.enable("false")) multiplexer_1 (
    .in0(not_10_out), .in1(adder_3_out), .out(multiplexer_1_out), .sel(adder_7_cout));
  Multiplexer #(.enable("false")) multiplexer_2 (
    .in0(not_11_out), .in1(adder_5_out), .out(multiplexer_2_out), .sel(adder_7_cout));
  and and_14 (and_14_out, b0, or_4_out, b1);
  Multiplexer #(.select(2), .enable("false")) multiplexer_3 (
    .in0(in_7), .in1(or_2_out), .in2(adder_8_cout), .in3(and_5_out), .out(y3), .sel(s1s0));
  Multiplexer #(.select(2), .enable("false")) multiplexer_4 (
    .in0(adder_4_cout), .in1(in_7), .in2(adder_8_out), .in3(or_1_out), .out(y2), .sel(s1s0));
  Multiplexer #(.select(2), .enable("false")) multiplexer_5 (
    .in0(adder_4_out), .in1(multiplexer_2_out), .in2(adder_6_out), .in3(and_13_out), .out(y1), .sel(s1s0));
  Multiplexer #(.select(2), .enable("false")) multiplexer_6 (
    .in0(adder_1_out), .in1(multiplexer_1_out), .in2(and_2_out), .in3(and_10_out), .out(y0), .sel(s1s0));
  Multiplexer #(.select(2), .enable("false")) multiplexer_7 (
    .in0(in_10), .in1(in_10), .in2(in_10), .in3(and_14_out), .out(recurring), .sel(s1s0));
endmodule
